# Fritzing sketch Drawing (saved by Fritzing 0.9.3b)
breadboards: 1

parts:
  Part1 = Arduino Uno (Rev3)
  L298N1 = L298N DC motor driver
  M1 = Getriebemotor
  M2 = Getriebemotor
  VCC1 = Battery  # not connected
  J1 = Basic Servo
  J2 = Basic Servo
  Part3 = Bluetooth HC-05 Macho
  R1 = Resistor [tolerance=±5% resistance=220 package="0402 [SMD]"]
  R2 = Resistor [tolerance=±5% resistance=220 package="0402 [SMD]"]
  M3 = RioRand LM2596

nets:
  N1: Part1.D8, L298N1.IN3
  N2: Part1.D9_PWM, L298N1.IN2
  N3: Part1.D10_PWM/SS, L298N1.IN1
  N4: Part1.D11_PWM/MOSI, L298N1.ENA
  N5: Part1.D0/RX, Part3.TXD
  N6: Part1.D1/TX, R1.Pin_0
  N7: Part1.D2, J1.pulse
  N8: Part1.D3_PWM, J2.pulse
  N9: Part1.D6_PWM, L298N1.ENB
  N10: Part1.D7, L298N1.IN4
  5V: Part1.5V, L298N1.5V
  GND: Part1.GND, L298N1.GND, J1.gnd, J2.gnd, M3.Pin_4
  N11: L298N1.OUT1, M2.pin_2
  N12: L298N1.OUT2, M2.pin_1
  N13: L298N1.OUT3, M1.pin_2
  N14: L298N1.OUT4, M1.pin_1
  VCC: J1.vcc, J2.vcc, M3.Pin_3
  N15: Part3.RXD, R1.Pin_1
  N16: Part3.GND, R2.Pin_0

notes:
  8 X AA NiMH Batteries (9.6V) 2000 mAh
  2 X MG90D Servo - Turret Ccontrol
  1k and 2k resistors into the TX pin of the HC-05. 2k resistor is the one going to ground.
  9.6V IN -> 5V OUT

custom parts:
  L298N DC motor driver: 2x DC motor driver with 78M05 positive voltage regulator (7..35 V) L298N: max 46 V, 2 A Set 5 V Enable jumper to enable 5 V regultor (needed for the L298N) and +5 V output at screw terminal or supply external +5 V at screw terminal Set ENA and/or ENB to +5 V to enable motor permanently or supply ENA and/or ENB with PWM signal IN1 and IN2 set rotation directory for motor A (OUT1/OUT2) IN2 and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
